// Logisim project TTL_Lib.circ as structural Verilog: 10 circuits, main circuit TTL7490
module INFO (
  input  tomasz,
  input  at,
  input  obuchowski,
  output dot,
  output net,
  output d0t,
  output pl
);

  wire and_1_out, and_2_out, and_3_out;

  and and_1 (and_1_out, ~tomasz, at, ~obuchowski);  // AND_Gate
  and and_2 (and_2_out, tomasz, at, obuchowski);
  and and_3 (and_3_out, tomasz, ~and_2_out);  // AND_Gate
  or or_1 (d0t, and_1_out, and_3_out);

  assign dot = tomasz;
  assign net = tomasz;
  assign pl = tomasz;
endmodule

module TTL7475 (
  input  D1,
  input  LE12,
  input  D2,
  input  D3,
  input  LE34,
  input  D4,
  output Q1,
  output NQ1,
  output Q2,
  output NQ2,
  output Q3,
  output NQ3,
  output Q4,
  output NQ4
);

  D_Flip_Flop #(.trigger("high")) d_ff_1 (.D(D1), .clk(LE12), .Q(Q1), .Qn(NQ1));  // open: preset, reset
  D_Flip_Flop #(.trigger("high")) d_ff_2 (.D(D2), .clk(LE12), .Q(Q2), .Qn(NQ2));  // open: preset, reset
  D_Flip_Flop #(.trigger("high")) d_ff_3 (.D(D3), .clk(LE34), .Q(Q3), .Qn(NQ3));  // open: preset, reset
  D_Flip_Flop #(.trigger("high")) d_ff_4 (.D(D4), .clk(LE34), .Q(Q4), .Qn(NQ4));  // open: preset, reset
endmodule

module TTL7483 (
  input  B4,
  input  A4,
  input  B3,
  input  A3,
  input  B2,
  input  A2,
  input  B1,
  input  A1,
  input  C0,
  output C4,
  output S4,
  output S3,
  output S2,
  output S1
);

  wire and_1_out, and_2_out, and_3_out, and_4_out, and_5_out, and_6_out, and_7_out, and_8_out, and_9_out,
       and_10_out, and_11_out, and_12_out, and_13_out, and_14_out, nand_1_out, nand_2_out, nand_3_out,
       nand_4_out, nor_1_out, nor_2_out, nor_3_out, nor_4_out, nor_6_out, nor_7_out, nor_8_out, not_1_out,
       not_2_out;

  nand nand_1 (nand_1_out, B4, A4);
  nor nor_1 (nor_1_out, B4, A4);
  nand nand_2 (nand_2_out, B3, A3);
  nor nor_2 (nor_2_out, B3, A3);
  nand nand_3 (nand_3_out, B2, A2);
  nor nor_3 (nor_3_out, B2, A2);
  nand nand_4 (nand_4_out, B1, A1);
  nor nor_4 (nor_4_out, B1, A1);
  not not_1 (not_1_out, C0);
  not not_2 (not_2_out, not_1_out);
  and and_1 (and_1_out, nor_2_out, nand_1_out);
  and and_2 (and_2_out, nor_3_out, nand_1_out, nand_2_out);
  and and_3 (and_3_out, nor_4_out, nand_1_out, nand_2_out, nand_3_out);
  and and_4 (and_4_out, nand_1_out, nand_2_out, nand_3_out, nand_4_out, not_1_out);
  and and_5 (and_5_out, nand_1_out, ~nor_1_out);  // AND_Gate
  and and_6 (and_6_out, nor_3_out, nand_2_out);
  and and_7 (and_7_out, nor_4_out, nand_2_out, nand_3_out);
  and and_8 (and_8_out, nand_2_out, nand_3_out, nand_4_out, not_1_out);
  and and_9 (and_9_out, nand_2_out, ~nor_2_out);  // AND_Gate
  and and_10 (and_10_out, nor_4_out, nand_3_out);
  and and_11 (and_11_out, nand_3_out, nand_4_out, not_1_out);
  and and_12 (and_12_out, nand_3_out, ~nor_3_out);  // AND_Gate
  and and_13 (and_13_out, nand_4_out, not_1_out);
  and and_14 (and_14_out, nand_4_out, ~nor_4_out);  // AND_Gate
  nor nor_5 (C4, nor_1_out, and_1_out, and_2_out, and_3_out, and_4_out);
  nor nor_6 (nor_6_out, nor_2_out, and_6_out, and_7_out, and_8_out);
  nor nor_7 (nor_7_out, nor_3_out, and_10_out, and_11_out);
  nor nor_8 (nor_8_out, nor_4_out, and_13_out);
  xor xor_1 (S4, and_5_out, nor_6_out);
  xor xor_2 (S3, and_9_out, nor_7_out);
  xor xor_3 (S2, and_12_out, nor_8_out);
  xor xor_4 (S1, and_14_out, not_2_out);
endmodule

module TTL7490 (
  input  A,
  input  B,
  input  R1,
  input  R2,
  input  R9_1,
  input  R9_2,
  output QA,
  output QB,
  output QC,
  output QD
);

  wire and_1_out, nand_1_out, nand_2_out, not_1_out, not_2_out, not_3_out, or_1_out, or_2_out, s_r_ff_1_qn;

  J_K_Flip_Flop #(.trigger("falling")) j_k_ff_1 (
    .J(1'b1), .K(1'b1), .clk(A), .Q(QA), .preset(not_2_out), .reset(not_1_out));  // open: Qn
  not not_1 (not_1_out, nand_1_out);
  nand nand_1 (nand_1_out, R1, R2);
  J_K_Flip_Flop #(.trigger("falling")) j_k_ff_2 (
    .J(s_r_ff_1_qn), .K(1'b1), .clk(B), .Q(QB), .reset(or_1_out));  // open: Qn, preset
  or or_1 (or_1_out, ~nand_1_out, ~nand_2_out);  // OR_Gate
  J_K_Flip_Flop #(.trigger("falling")) j_k_ff_3 (
    .J(1'b1), .K(1'b1), .clk(QB), .Q(QC), .reset(or_2_out));  // open: Qn, preset
  or or_2 (or_2_out, ~nand_1_out, ~nand_2_out);  // OR_Gate
  not not_2 (not_2_out, nand_2_out);
  S_R_Flip_Flop #(.trigger("falling")) s_r_ff_1 (
    .S(and_1_out), .R(QD), .clk(B), .Q(QD), .reset(not_3_out), .Qn(s_r_ff_1_qn), .preset(not_2_out));
  and and_1 (and_1_out, QB, QC);
  not not_3 (not_3_out, nand_1_out);
  nand nand_2 (nand_2_out, R9_1, R9_2);
endmodule

module TTL7492 (
  input  A,
  input  B,
  input  R1,
  input  R2,
  output QA,
  output QB,
  output QC,
  output QD
);

  wire and_1_out, j_k_ff_3_qn;

  J_K_Flip_Flop #(.trigger("falling")) j_k_ff_1 (
    .J(1'b1), .K(1'b1), .clk(A), .Q(QA), .reset(and_1_out));  // open: Qn, preset
  J_K_Flip_Flop #(.trigger("falling")) j_k_ff_2 (
    .J(j_k_ff_3_qn), .K(1'b1), .clk(B), .Q(QB), .reset(and_1_out));  // open: Qn, preset
  J_K_Flip_Flop #(.trigger("falling")) j_k_ff_3 (
    .J(QB), .K(1'b1), .clk(B), .Q(QC), .Qn(j_k_ff_3_qn), .reset(and_1_out));  // open: preset
  and and_1 (and_1_out, R1, R2);
  J_K_Flip_Flop #(.trigger("falling")) j_k_ff_4 (
    .J(1'b1), .K(1'b1), .clk(QC), .Q(QD), .reset(and_1_out));  // open: Qn, preset
endmodule

module TTL7493 (
  input  A,
  input  B,
  input  R1,
  input  R2,
  output QA,
  output QB,
  output QC,
  output QD
);

  wire and_1_out;

  J_K_Flip_Flop #(.trigger("falling")) j_k_ff_1 (
    .J(1'b1), .K(1'b1), .clk(A), .Q(QA), .reset(and_1_out));  // open: Qn, preset
  J_K_Flip_Flop #(.trigger("falling")) j_k_ff_2 (
    .J(1'b1), .K(1'b1), .clk(B), .Q(QB), .reset(and_1_out));  // open: Qn, preset
  J_K_Flip_Flop #(.trigger("falling")) j_k_ff_3 (
    .J(1'b1), .K(1'b1), .clk(QB), .Q(QC), .reset(and_1_out));  // open: Qn, preset
  and and_1 (and_1_out, R1, R2);
  J_K_Flip_Flop #(.trigger("falling")) j_k_ff_4 (
    .J(1'b1), .K(1'b1), .clk(QC), .Q(QD), .reset(and_1_out));  // open: Qn, preset
endmodule

module TTL7495 (
  input  A,
  input  B,
  input  C,
  input  D,
  input  MODE,
  input  SER,
  input  CLK1,
  input  CLK2,
  output Q_A,
  output Q_B,
  output Q_C,
  output Q_D
);

  wire and_1_out, and_2_out, and_3_out, and_4_out, and_5_out, and_6_out, and_7_out, and_8_out, and_9_out,
       and_10_out, nor_1_out, nor_2_out, nor_3_out, nor_4_out, not_1_out, not_2_out, not_3_out, not_4_out,
       not_5_out, not_6_out, or_1_out;

  not not_1 (not_1_out, MODE);
  not not_2 (not_2_out, not_1_out);
  and and_1 (and_1_out, SER, not_1_out);
  and and_2 (and_2_out, not_1_out, CLK1);
  and and_3 (and_3_out, MODE, CLK2);
  and and_4 (and_4_out, not_2_out, A);
  nor nor_1 (nor_1_out, and_1_out, and_4_out);
  not not_3 (not_3_out, nor_1_out);
  S_R_Flip_Flop #(.trigger("falling")) s_r_ff_1 (
    .S(not_3_out), .R(nor_1_out), .clk(or_1_out), .Q(Q_A));  // open: reset, Qn, preset
  or or_1 (or_1_out, and_2_out, and_3_out);
  and and_5 (and_5_out, Q_A, not_1_out);
  and and_6 (and_6_out, not_2_out, B);
  nor nor_2 (nor_2_out, and_5_out, and_6_out);
  not not_4 (not_4_out, nor_2_out);
  S_R_Flip_Flop #(.trigger("falling")) s_r_ff_2 (
    .S(not_4_out), .R(nor_2_out), .clk(or_1_out), .Q(Q_B));  // open: reset, Qn, preset
  and and_7 (and_7_out, Q_B, not_1_out);
  nor nor_3 (nor_3_out, and_7_out, and_8_out);
  not not_5 (not_5_out, nor_3_out);
  and and_8 (and_8_out, not_2_out, C);
  S_R_Flip_Flop #(.trigger("falling")) s_r_ff_3 (
    .S(not_5_out), .R(nor_3_out), .clk(or_1_out), .Q(Q_C));  // open: reset, Qn, preset
  and and_9 (and_9_out, Q_C, not_1_out);
  nor nor_4 (nor_4_out, and_9_out, and_10_out);
  and and_10 (and_10_out, not_2_out, D);
  not not_6 (not_6_out, nor_4_out);
  S_R_Flip_Flop #(.trigger("falling")) s_r_ff_4 (
    .S(not_6_out), .R(nor_4_out), .clk(or_1_out), .Q(Q_D));  // open: reset, Qn, preset
endmodule

module TTL74164 (
  input  DSA,
  input  DSB,
  input  CP,
  input  NMR,
  output Q0,
  output Q1,
  output Q2,
  output Q3,
  output Q4,
  output Q5,
  output Q6,
  output Q7
);

  wire and_1_out, not_1_out, not_2_out;

  and and_1 (and_1_out, DSA, DSB);
  not not_1 (not_1_out, CP);
  not not_2 (not_2_out, NMR);
  D_Flip_Flop #(.trigger("falling")) d_ff_1 (
    .D(and_1_out), .clk(not_1_out), .Q(Q0), .reset(not_2_out));  // open: Qn, preset
  D_Flip_Flop #(.trigger("falling")) d_ff_2 (.D(Q0), .clk(not_1_out), .Q(Q1), .reset(not_2_out));  // open: Qn, preset
  D_Flip_Flop #(.trigger("falling")) d_ff_3 (.D(Q1), .clk(not_1_out), .Q(Q2), .reset(not_2_out));  // open: Qn, preset
  D_Flip_Flop #(.trigger("falling")) d_ff_4 (.D(Q2), .clk(not_1_out), .Q(Q3), .reset(not_2_out));  // open: Qn, preset
  D_Flip_Flop #(.trigger("falling")) d_ff_5 (.D(Q3), .clk(not_1_out), .Q(Q4), .reset(not_2_out));  // open: Qn, preset
  D_Flip_Flop #(.trigger("falling")) d_ff_6 (.D(Q4), .clk(not_1_out), .Q(Q5), .reset(not_2_out));  // open: Qn, preset
  D_Flip_Flop #(.trigger("falling")) d_ff_7 (.D(Q5), .clk(not_1_out), .Q(Q6), .reset(not_2_out));  // open: Qn, preset
  D_Flip_Flop #(.trigger("falling")) d_ff_8 (.D(Q6), .clk(not_1_out), .Q(Q7), .reset(not_2_out));  // open: Qn, preset
endmodule

module TTL74190 (
  input  D0,
  input  D1,
  input  D2,
  input  D3,
  input  NPL,
  input  NU_D,
  input  NCE,
  input  CP,
  output NRC,
  output TC,
  output Q0,
  output Q1,
  output Q2,
  output Q3
);

  wire and_1_out, and_2_out, and_3_out, and_4_out, and_5_out, and_6_out, and_7_out, and_8_out, and_9_out,
       and_10_out, and_11_out, j_k_ff_1_qn, j_k_ff_2_qn, j_k_ff_3_qn, j_k_ff_4_qn, nand_2_out, nand_3_out,
       nand_4_out, nand_5_out, nand_6_out, nand_7_out, nand_8_out, nand_9_out, nand_10_out, not_1_out,
       not_2_out, not_3_out, not_4_out, not_5_out, not_6_out, not_7_out, not_8_out, not_9_out, not_10_out,
       not_11_out, not_12_out, not_13_out, or_2_out, or_3_out, or_4_out;

  not not_1 (not_1_out, NPL);
  not not_2 (not_2_out, NU_D);
  not not_3 (not_3_out, CP);
  and and_1 (and_1_out, ~not_4_out, ~NCE);  // AND_Gate
  and and_2 (and_2_out, ~NCE, ~not_2_out);  // AND_Gate
  not not_4 (not_4_out, not_2_out);
  not not_5 (not_5_out, NCE);
  and and_3 (and_3_out, not_2_out, Q0, Q3);
  nand nand_1 (NRC, not_5_out, not_3_out, TC);
  and and_4 (and_4_out, not_4_out, j_k_ff_1_qn, j_k_ff_2_qn, j_k_ff_3_qn, j_k_ff_4_qn);
  or or_1 (TC, and_3_out, and_4_out);
  nand nand_2 (nand_2_out, D0, not_1_out);
  not not_6 (not_6_out, nand_2_out);
  J_K_Flip_Flop #(.trigger("falling")) j_k_ff_1 (
    .J(not_5_out), .K(not_5_out), .clk(not_3_out), .Q(Q0), .Qn(j_k_ff_1_qn), .preset(not_6_out),
    .reset(not_7_out));
  not not_7 (not_7_out, nand_3_out);
  nand nand_3 (nand_3_out, nand_2_out, not_1_out);
  nand nand_4 (nand_4_out, D1, not_1_out);
  and and_5 (and_5_out, and_2_out, j_k_ff_1_qn, nand_5_out);
  or or_2 (or_2_out, and_5_out, and_6_out);
  not not_8 (not_8_out, nand_4_out);
  J_K_Flip_Flop #(.trigger("falling")) j_k_ff_2 (
    .J(or_2_out), .K(or_2_out), .clk(not_3_out), .Q(Q1), .Qn(j_k_ff_2_qn), .preset(not_8_out),
    .reset(not_9_out));
  not not_9 (not_9_out, nand_6_out);
  and and_6 (and_6_out, Q0, j_k_ff_4_qn, and_1_out);
  nand nand_5 (nand_5_out, j_k_ff_2_qn, j_k_ff_3_qn, j_k_ff_4_qn);
  nand nand_6 (nand_6_out, nand_4_out, not_1_out);
  and and_7 (and_7_out, nand_5_out, and_2_out, j_k_ff_1_qn, j_k_ff_2_qn);
  nand nand_7 (nand_7_out, D2, not_1_out);
  J_K_Flip_Flop #(.trigger("falling")) j_k_ff_3 (
    .J(or_3_out), .K(or_3_out), .clk(not_3_out), .Q(Q2), .Qn(j_k_ff_3_qn), .preset(not_10_out),
    .reset(not_11_out));
  and and_8 (and_8_out, Q0, Q1, and_1_out);
  or or_3 (or_3_out, and_7_out, and_8_out);
  not not_10 (not_10_out, nand_7_out);
  not not_11 (not_11_out, nand_8_out);
  nand nand_8 (nand_8_out, nand_7_out, not_1_out);
  nand nand_9 (nand_9_out, D3, not_1_out);
  and and_9 (and_9_out, and_2_out, j_k_ff_1_qn, j_k_ff_2_qn, j_k_ff_3_qn);
  J_K_Flip_Flop #(.trigger("falling")) j_k_ff_4 (
    .J(or_4_out), .K(or_4_out), .clk(not_3_out), .Q(Q3), .Qn(j_k_ff_4_qn), .preset(not_12_out),
    .reset(not_13_out));
  and and_10 (and_10_out, Q0, Q3, and_1_out);
  or or_4 (or_4_out, and_9_out, and_10_out, and_11_out);
  not not_12 (not_12_out, nand_9_out);
  not not_13 (not_13_out, nand_10_out);
  and and_11 (and_11_out, Q0, Q1, Q2, and_1_out);
  nand nand_10 (nand_10_out, nand_9_out, not_1_out);
endmodule

module TTL74198 (
  input  CP,
  input  DSR,
  input  S1,
  input  S0,
  input  D0,
  input  D1,
  input  D2,
  input  D3,
  input  D4,
  input  D5,
  input  D6,
  input  D7,
  input  DSL,
  input  NMR,
  output Q0,
  output Q1,
  output Q2,
  output Q3,
  output Q4,
  output Q5,
  output Q6,
  output Q7
);

  wire and_1_out, and_2_out, and_3_out, and_4_out, and_5_out, and_6_out, and_7_out, and_8_out, and_9_out,
       and_10_out, and_11_out, and_12_out, and_13_out, and_14_out, and_15_out, and_16_out, and_17_out,
       and_18_out, and_19_out, and_20_out, and_21_out, and_22_out, and_23_out, and_24_out, and_25_out,
       and_26_out, and_27_out, nand_1_out, nor_1_out, nor_2_out, nor_3_out, nor_4_out, nor_5_out, nor_6_out,
       nor_7_out, nor_8_out, nor_9_out, not_1_out, not_2_out, not_3_out, not_4_out, not_5_out, not_6_out,
       not_7_out, not_8_out, not_9_out, not_10_out, not_11_out;

  not not_1 (not_1_out, S1);
  not not_2 (not_2_out, S0);
  and and_1 (and_1_out, CP, ~nor_1_out);  // AND_Gate
  and and_2 (and_2_out, not_2_out, not_1_out);
  and and_3 (and_3_out, ~not_1_out, ~not_2_out);  // AND_Gate
  nor nor_1 (nor_1_out, and_1_out, and_2_out);
  not not_3 (not_3_out, NMR);
  nand nand_1 (nand_1_out, CP, nor_1_out);
  and and_4 (and_4_out, DSR, not_1_out);
  and and_5 (and_5_out, and_3_out, D0);
  and and_6 (and_6_out, not_2_out, Q1);
  and and_7 (and_7_out, Q0, not_1_out);
  and and_8 (and_8_out, and_3_out, D1);
  and and_9 (and_9_out, not_2_out, Q2);
  and and_10 (and_10_out, Q1, not_1_out);
  and and_11 (and_11_out, and_3_out, D2);
  and and_12 (and_12_out, not_2_out, Q3);
  and and_13 (and_13_out, Q2, not_1_out);
  and and_14 (and_14_out, and_3_out, D3);
  and and_15 (and_15_out, not_2_out, Q4);
  and and_16 (and_16_out, Q3, not_1_out);
  and and_17 (and_17_out, and_3_out, D4);
  and and_18 (and_18_out, not_2_out, Q5);
  and and_19 (and_19_out, Q4, not_1_out);
  and and_20 (and_20_out, and_3_out, D5);
  and and_21 (and_21_out, not_2_out, Q6);
  and and_22 (and_22_out, Q5, not_1_out);
  and and_23 (and_23_out, and_3_out, D6);
  and and_24 (and_24_out, not_2_out, Q7);
  and and_25 (and_25_out, Q6, not_1_out);
  and and_26 (and_26_out, and_3_out, D7);
  and and_27 (and_27_out, not_2_out, DSL);
  nor nor_2 (nor_2_out, and_4_out, and_5_out, and_6_out);
  nor nor_3 (nor_3_out, and_7_out, and_8_out, and_9_out);
  nor nor_4 (nor_4_out, and_10_out, and_11_out, and_12_out);
  nor nor_5 (nor_5_out, and_13_out, and_14_out, and_15_out);
  nor nor_6 (nor_6_out, and_16_out, and_17_out, and_18_out);
  nor nor_7 (nor_7_out, and_19_out, and_20_out, and_21_out);
  nor nor_8 (nor_8_out, and_22_out, and_23_out, and_24_out);
  nor nor_9 (nor_9_out, and_25_out, and_26_out, and_27_out);
  not not_4 (not_4_out, nor_2_out);
  not not_5 (not_5_out, nor_3_out);
  not not_6 (not_6_out, nor_4_out);
  not not_7 (not_7_out, nor_5_out);
  not not_8 (not_8_out, nor_6_out);
  not not_9 (not_9_out, nor_7_out);
  not not_10 (not_10_out, nor_8_out);
  not not_11 (not_11_out, nor_9_out);
  S_R_Flip_Flop #(.trigger("falling")) s_r_ff_1 (
    .S(not_4_out), .R(nor_2_out), .clk(nand_1_out), .Q(Q0), .reset(not_3_out));  // open: Qn, preset
  S_R_Flip_Flop #(.trigger("falling")) s_r_ff_2 (
    .S(not_5_out), .R(nor_3_out), .clk(nand_1_out), .Q(Q1), .reset(not_3_out));  // open: Qn, preset
  S_R_Flip_Flop #(.trigger("falling")) s_r_ff_3 (
    .S(not_6_out), .R(nor_4_out), .clk(nand_1_out), .Q(Q2), .reset(not_3_out));  // open: Qn, preset
  S_R_Flip_Flop #(.trigger("falling")) s_r_ff_4 (
    .S(not_7_out), .R(nor_5_out), .clk(nand_1_out), .Q(Q3), .reset(not_3_out));  // open: Qn, preset
  S_R_Flip_Flop #(.trigger("falling")) s_r_ff_5 (
    .S(not_8_out), .R(nor_6_out), .clk(nand_1_out), .Q(Q4), .reset(not_3_out));  // open: Qn, preset
  S_R_Flip_Flop #(.trigger("falling")) s_r_ff_6 (
    .S(not_9_out), .R(nor_7_out), .clk(nand_1_out), .Q(Q5), .reset(not_3_out));  // open: Qn, preset
  S_R_Flip_Flop #(.trigger("falling")) s_r_ff_7 (
    .S(not_10_out), .R(nor_8_out), .clk(nand_1_out), .Q(Q6), .reset(not_3_out));  // open: Qn, preset
  S_R_Flip_Flop #(.trigger("falling")) s_r_ff_8 (
    .S(not_11_out), .R(nor_9_out), .clk(nand_1_out), .Q(Q7), .reset(not_3_out));  // open: Qn, preset
endmodule
